# Fritzing sketch mini_mixer-02 (saved by Fritzing 0.9.2b)
breadboards: 1

parts:
  IC1 = Dual Op-Amp [package=dip08]
  R1 = Rotary Potentiometer (Small) [maximum_resistance=100kΩ package=THT]
  C1 = Ceramic Capacitor [capacitance=100nF package="100 mil [THT, multilayer]"]
  R2 = Resistor [tolerance=±5% resistance=47k package=THT]
  C2 = Ceramic Capacitor [capacitance=100nF package="100 mil [THT, multilayer]"]
  R3 = Resistor [tolerance=±5% resistance=47k package=THT]
  C3 = Ceramic Capacitor [capacitance=100nF package="100 mil [THT, multilayer]"]
  R4 = Resistor [tolerance=±5% resistance=47k package=THT]
  J1 = female pin header, 1 pin [form="♀ (female)"]
  C4 = Ceramic Capacitor [capacitance=100nF package="100 mil [THT, multilayer]"]
  C5 = Ceramic Capacitor [capacitance=100nF package="100 mil [THT, multilayer]"]
  R5 = Resistor [tolerance=±5% resistance=100k package=THT]
  R6 = Resistor [tolerance=±5% resistance=22k package=THT]
  R7 = Resistor [tolerance=±5% resistance=22k package=THT]
  C6 = Electrolytic Capacitor [capacitance=1µF package="100 mil [THT, electrolytic]"]
  C7 = Electrolytic Capacitor [capacitance=1µF package="100 mil [THT, electrolytic]"]
  C8 = Electrolytic Capacitor [capacitance=1µF package="100 mil [THT, electrolytic]"]
  J2 = female pin header, 1 pin [form="♀ (female)"]
  R8 = Resistor [tolerance=±5% resistance=22k package=THT]
  R9 = Resistor [tolerance=±5% resistance=22k package=THT]
  J3 = female pin header, 1 pin [form="♀ (female)"]
  R10 = Resistor [tolerance=±5% resistance=15k package=THT]
  R11 = Resistor [tolerance=±5% resistance=33k package=THT]
  J4 = female pin header, 1 pin [form="♀ (female)"]
  R12 = Resistor [tolerance=±5% resistance=4.7k package=THT]
  LED1 = LED - 5mm [color="Blue (525nm)" package="5 mm [THT]"]

nets:
  N1: IC1.A_OUT, IC1.A_-IN, IC1.B_+IN, R1.leg2, C4.0, C5.1, C7.-, C8.+, R9.Pin_1, R11.Pin_1
  N2: IC1.A_+IN, R6.Pin_1, R7.Pin_0
  N3: IC1.A_V-, C5.0, R7.Pin_1, C6.-, C8.-, LED1.cathode
  N4: IC1.B_-IN, R2.Pin_1, R3.Pin_1, R4.Pin_1, R5.Pin_1
  N5: IC1.B_OUT, R5.Pin_0, J2.pin1
  N6: IC1.A_V+, C4.1, R6.Pin_0, C6.+, C7.+, R12.Pin_0
  N7: R1.leg1, J1.pin1
  N8: R1.wiper, C1.0
  N9: C1.1, R2.Pin_0
  N10: C2.0, R8.Pin_1, R9.Pin_0
  N11: C2.1, R3.Pin_0
  N12: C3.0, R10.Pin_1, R11.Pin_0
  N13: C3.1, R4.Pin_0
  N14: R8.Pin_0, J3.pin1
  N15: R10.Pin_0, J4.pin1
  N16: R12.Pin_1, LED1.anode

notes:
  VGND
  +5V
  0V
  VGND
