# Fritzing sketch mini_mixer (saved by Fritzing 0.9.2b)
breadboards: 1

parts:
  IC1 = Dual Op-Amp [package=dip08]
  R5 = Resistor [tolerance=±5% resistance=4.7k package=THT]
  R6 = Resistor [tolerance=±5% resistance=4.7k package=THT]
  J3 = female pin header, 1 pin [form="♀ (female)"]
  C3 = Ceramic Capacitor [capacitance=100nF package="100 mil [THT, multilayer]"]
  C4 = Ceramic Capacitor [capacitance=100nF package="100 mil [THT, multilayer]"]
  C5 = Ceramic Capacitor [capacitance=100nF package="100 mil [THT, multilayer]"]
  R7 = Resistor [tolerance=±5% resistance=47k package=THT]
  R8 = Resistor [tolerance=±5% resistance=47k package=THT]
  R9 = Resistor [tolerance=±5% resistance=47k package=THT]
  R10 = Resistor [tolerance=±5% resistance=100k package=THT]
  R11 = Resistor [tolerance=±5% resistance=10k package=THT]
  R12 = Resistor [tolerance=±5% resistance=10k package=THT]
  J4 = female pin header, 1 pin [form="♀ (female)"]
  R13 = Rotary Potentiometer (Small) [maximum_resistance=100kΩ package=THT]
  R14 = Rotary Potentiometer (Small) [maximum_resistance=100kΩ package=THT]
  J5 = female pin header, 1 pin [form="♀ (female)"]
  J6 = female pin header, 1 pin [form="♀ (female)"]
  R15 = Resistor [tolerance=±5% resistance=47 package=THT]
  C6 = Ceramic Capacitor [capacitance=100nF package="100 mil [THT, multilayer]"]
  C7 = Ceramic Capacitor [capacitance=100nF package="100 mil [THT, multilayer]"]

nets:
  N1: IC1.A_OUT, R10.Pin_1, R11.Pin_1
  N2: IC1.A_-IN, R7.Pin_1, R8.Pin_1, R9.Pin_1, R10.Pin_0
  N3: IC1.A_+IN, IC1.B_+IN, R6.Pin_1, R13.leg1, R14.leg1, C6.0, C7.1
  N4: IC1.A_V-, C7.0
  N5: IC1.B_-IN, R11.Pin_0, R12.Pin_1
  N6: IC1.B_OUT, R12.Pin_0, R15.Pin_1
  N7: IC1.A_V+, C6.1
  N8: R5.Pin_0, J3.pin1
  N9: R5.Pin_1, R6.Pin_0, C5.0
  N10: C3.0, R13.wiper
  N11: C3.1, R7.Pin_0
  N12: C4.0, R14.wiper
  N13: C4.1, R8.Pin_0
  N14: C5.1, R9.Pin_0
  N15: J4.pin1, R15.Pin_0
  N16: R13.leg2, J5.pin1
  N17: R14.leg2, J6.pin1

notes:
  GND
  VCC
  VEE
  GND
